// Logisim project army_hard_coding_competition.circ as structural Verilog
module _4_Bit_Ripple_adder (
  input  A0,
  input  A1,
  input  A2,
  input  A3,
  input  B1,
  input  B2,
  input  B3,
  input  B0,
  output Cout,
  output Y0,
  output Y1,
  output Y2,
  output Y3
);

  wire full_adder_1_cout, full_adder_2_cout, full_adder_3_cout;

  full_adder full_adder_1 (.Cin(1'b0), .Y(A0), .Z(B0), .SUM(Y0), .Cout(full_adder_1_cout));
  full_adder full_adder_2 (.Cin(full_adder_1_cout), .Y(A1), .Z(B1), .SUM(Y1), .Cout(full_adder_2_cout));
  full_adder full_adder_3 (.Cin(full_adder_2_cout), .Y(A2), .Z(B2), .SUM(Y2), .Cout(full_adder_3_cout));
  full_adder full_adder_4 (.Cin(full_adder_3_cout), .Y(A3), .Z(B3), .SUM(Y3), .Cout(Cout));
endmodule

module bin_multiplie_4bit_input (
  input  A,
  input  B,
  input  C,
  input  D,
  input  E,
  input  F,
  input  G,
  input  H,
  output u,
  output v,
  output w,
  output x,
  output q,
  output r,
  output s,
  output t,
  output m,
  output n,
  output o,
  output p,
  output i,
  output j,
  output k,
  output l
);

  and and_1 (u, E, A);
  and and_2 (v, E, B);
  and and_3 (w, E, C);
  and and_4 (x, E, D);
  and and_5 (q, F, A);
  and and_6 (r, F, B);
  and and_7 (s, F, C);
  and and_8 (t, F, D);
  and and_9 (m, G, A);
  and and_10 (n, G, B);
  and and_11 (o, G, C);
  and and_12 (p, G, D);
  and and_13 (i, H, A);
  and and_14 (j, H, B);
  and and_15 (k, H, C);
  and and_16 (l, H, D);
endmodule

module full_adder (
  input  Cin,
  input  Y,
  input  Z,
  output SUM,
  output Cout
);

  wire and_1_out, and_2_out, and_3_out, xor_1_out;

  and and_1 (and_1_out, Z, Cin);
  and and_2 (and_2_out, Cin, Y);
  and and_3 (and_3_out, Y, Z);
  xor xor_1 (xor_1_out, Z, Y);
  xor xor_2 (SUM, xor_1_out, Cin);
  or or_1 (Cout, and_1_out, and_2_out, and_3_out);
endmodule

module _8_bit_ripple_adder (
  input  A0,
  input  A1,
  input  A2,
  input  A3,
  input  A4,
  input  A5,
  input  A6,
  input  A7,
  input  B0,
  input  B1,
  input  B2,
  input  B3,
  input  B4,
  input  B5,
  input  B6,
  input  B7,
  output Cout,
  output Y0,
  output Y1,
  output Y2,
  output Y3,
  output Y4,
  output Y5,
  output Y6,
  output Y7
);

  wire full_adder_1_cout, full_adder_2_cout, full_adder_3_cout, full_adder_4_cout, full_adder_5_cout,
       full_adder_6_cout, full_adder_7_cout;

  full_adder full_adder_1 (.Cin(1'b0), .Y(A0), .Z(B0), .SUM(Y0), .Cout(full_adder_1_cout));
  full_adder full_adder_2 (.Cin(full_adder_1_cout), .Y(A1), .Z(B1), .SUM(Y1), .Cout(full_adder_2_cout));
  full_adder full_adder_3 (.Cin(full_adder_2_cout), .Y(A2), .Z(B2), .SUM(Y2), .Cout(full_adder_3_cout));
  full_adder full_adder_4 (.Cin(full_adder_3_cout), .Y(A3), .Z(B3), .SUM(Y3), .Cout(full_adder_4_cout));
  full_adder full_adder_5 (.Cin(full_adder_4_cout), .Y(A4), .Z(B4), .SUM(Y4), .Cout(full_adder_5_cout));
  full_adder full_adder_6 (.Cin(full_adder_5_cout), .Y(A5), .Z(B5), .SUM(Y5), .Cout(full_adder_6_cout));
  full_adder full_adder_7 (.Cin(full_adder_6_cout), .Y(A6), .Z(B6), .SUM(Y6), .Cout(full_adder_7_cout));
  full_adder full_adder_8 (.Cin(full_adder_7_cout), .Y(A7), .Z(B7), .SUM(Y7), .Cout(Cout));
endmodule
